# Fritzing sketch TPA6139A2 (saved by Fritzing 0.9.2b)
breadboards: 1

parts:
  U1 = mystery part, 14 pins [chip_label=TPA6139A2]
  C1 = Ceramic Capacitor [capacitance=2.2µF package="100 mil [THT, multilayer]"]
  C2 = Ceramic Capacitor [capacitance=2.2µF package="100 mil [THT, multilayer]"]
  J1 = male pin header, 1 pin [form="♂ (male)"]
  J2 = male pin header, 1 pin [form="♂ (male)"]
  J3 = male pin header, 1 pin [form="♂ (male)"]
  J4 = male pin header, 1 pin [form="♂ (male)"]
  C3 = Ceramic Capacitor [capacitance=100nF package="100 mil [THT, multilayer]"]
  C4 = Ceramic Capacitor [capacitance=100nF package="100 mil [THT, multilayer]"]
  R1 = Resistor [tolerance=±5% resistance=47k package=THT]
  C5 = Ceramic Capacitor [capacitance=100nF package="100 mil [THT, multilayer]"]

nets:
  N1: U1.pin1, C1.1
  N2: U1.pin2, J4.pin1
  N3: U1.pin3, U1.pin11, C3.1, R1.Pin_0, C5.0
  N4: U1.pin4, U1.pin10, C5.1
  N5: U1.pin5, C3.0
  N6: U1.pin6, C4.0
  N7: U1.pin9, C4.1
  N8: U1.pin12, R1.Pin_1
  N9: U1.pin13, J3.pin1
  N10: U1.pin14, C2.1
  N11: C1.0, J1.pin1
  N12: C2.0, J2.pin1

notes:
  GND
  3.3V
